# Fritzing sketch GH (saved by Fritzing 1.0.6)
perfboards: 1

parts:
  A1 = Orange PI 3 LTS  # not connected
  Компонент1 = Arduino Mega 2560 (Rev3)
  J4 = Camdenboss CTB0158-3 [part_number=CTB0158-3 package=THT]
  J5 = Camdenboss CTB0158-3 [part_number=CTB0158-3 package=THT]
  J6 = Camdenboss CTB0158-3 [part_number=CTB0158-3 package=THT]
  J7 = double row female pin header, 14 pins [form="♀ (female)"]
  J8 = double row female pin header, 14 pins [form="♀ (female)"]
  R1 = Resistor [tolerance=±5% resistance=4.7k package="0603 [SMD]"]  # not connected
  R2 = Resistor [tolerance=±5% resistance=3.3k package="0603 [SMD]"]
  Компонент2 = Logic Level Converter
  J1 = female pin header, 10 pins [form="♀ (female)"]
  J9 = female pin header, 10 pins [form="♀ (female)"]
  J10 = male pin header, 3 pins [form="♂ (male)"]
  J11 = male pin header, 4 pins [form="♂ (male)"]
  J12 = male pin header, 4 pins [form="♂ (male)"]
  J13 = male pin header, 4 pins [form="♂ (male)"]
  J14 = male pin header, 2 pins [form="♂ (male)"]
  DS1 = DS18B20 1-Wire Temperature Sensor [part_number=DS18B20]
  U3 = 4-Channel 5v Relay Shield [package=relay-4ch5v10a]
  U4 = 4-Channel 5v Relay Shield [package=relay-4ch5v10a]

nets:
  N1: Компонент1.D19/RX1, J9.pin10, J10.pin2
  N2: Компонент1.D18/TX1, J9.pin9, J10.pin3
  N3: Компонент1.GND, Компонент2.TX_HV, Компонент2.RX_HV, J9.pin7, J9.pin8, J10.pin1, J11.pin1, J11.pin2, J11.pin3, J11.pin4, J14.pin1, J14.pin2
  N4: Компонент1.D22, U4.IN1
  N5: Компонент1.D24, U4.IN2
  N6: Компонент1.D26, U4.IN3
  N7: Компонент1.D28, U4.IN4
  N8: Компонент1.D30, U3.IN1
  N9: Компонент1.D32, U3.IN2
  N10: Компонент1.D34, U3.IN3
  N11: Компонент1.D36, U3.IN4
  N12: J4.pin1, J5.pin1, J6.pin1, J8.pin10, DS1.GND
  N13: J4.pin2, J5.pin2, J6.pin2, J8.pin11, R2.Pin_0, DS1.DQ
  N14: J4.pin3, J5.pin3, J6.pin3, R2.Pin_1, DS1.VDD
  N15: J7.pin13, Компонент2.HV, J9.pin6, J12.pin4
  N16: J7.pin14, J8.pin1, Компонент2.GND, J1.pin5, J9.pin5, J13.pin4
  N17: J8.pin5, Компонент2.LV, J1.pin6
  N18: J8.pin8, J1.pin10
  N19: J8.pin9, J1.pin9
  N20: J8.pin12, Компонент2.TX_LV, J1.pin8
  N21: J8.pin13, Компонент2.RX_LV, J1.pin7
  N22: Компонент2.TX2_LV, J1.pin3
  N23: Компонент2.RX2_LV, J1.pin4
  N24: Компонент2.RX2_HV, J9.pin4
  N25: Компонент2.TX2_HV, J9.pin3

notes:
  UART3
  GND/TX/RX
  I2C
  GND/5V/SCL/SDA
  PD22
  5V/S/GND
  UART1
  GND/RX/TX
  12V / GND
  5V / GND

custom parts:
  Orange PI 3 LTS: Orange Pi 3 LTS is an open-source single-board computer with dual-band wireless WiFi and Bluetooth 5.0 .It is highly compact with a dimension of 56X85mm.
  4-Channel 5v Relay Shield: 4 Channel 5v Relay Shield w. 2x SPD-06VDC-SD-C
